# Fritzing sketch wonky_drum_seq (saved by Fritzing 0.8.5b)
breadboards: 1

parts:
  Teensy2 = Teensy 2.0
  S1 = Pushbutton [package="[THT]"]
  S2 = Pushbutton [package="[THT]"]
  S3 = Pushbutton [package="[THT]"]
  S4 = Pushbutton [package="[THT]"]
  S5 = Pushbutton [package="[THT]"]
  R1 = Photocell (LDR) [package=THT]
  R2 = Photocell (LDR) [package=THT]
  R3 = Photocell (LDR) [package=THT]
  LED5 = LED - 3mm [color="Red (633nm)" package="3 mm [THT]"]
  R5 = Resistor [tolerance=±5% resistance=680 package=THT]
  R7 = Resistor [tolerance=±5% resistance=680 package=THT]
  R8 = Resistor [tolerance=±5% resistance=680 package=THT]
  R9 = Resistor [tolerance=±5% resistance=680 package=THT]
  R10 = Resistor [tolerance=±5% resistance=680 package=THT]
  R11 = Resistor [tolerance=±5% resistance=680 package=THT]
  R12 = Resistor [tolerance=±5% resistance=680 package=THT]
  R13 = Resistor [tolerance=±5% resistance=4.7k package=THT]
  R14 = Resistor [tolerance=±5% resistance=680 package=THT]
  LED6 = LED - 3mm [color="Red (633nm)" package="3 mm [THT]"]
  LED7 = LED - 3mm [color="Red (633nm)" package="3 mm [THT]"]
  LED8 = LED - 3mm [color="Red (633nm)" package="3 mm [THT]"]
  LED9 = LED - 3mm [color="Red (633nm)" package="3 mm [THT]"]
  R15 = Rotary Potentiometer (Small) [maximum_resistance=10kΩ package=THT]

nets:
  N1: Teensy2.GND, S1.Pin_3, S1.Pin_4, S2.Pin_3, S2.Pin_4, S3.Pin_3, S3.Pin_4, S4.Pin_3, S4.Pin_4, S5.Pin_3, S5.Pin_4, LED5.cathode, LED6.cathode, LED7.cathode, LED8.cathode, LED9.cathode
  N2: Teensy2.B0, S5.Pin_1, S5.Pin_2
  N3: Teensy2.B1, S4.Pin_1, S4.Pin_2
  N4: Teensy2.B2, S3.Pin_1, S3.Pin_2
  N5: Teensy2.B3, S1.Pin_1, S1.Pin_2
  N6: Teensy2.B7, R8.Pin_0
  N7: Teensy2.D0, R9.Pin_0
  N8: Teensy2.D1, S2.Pin_1, S2.Pin_2
  N9: Teensy2.D2, R7.Pin_0
  N10: Teensy2.D3, R14.Pin_0
  N11: Teensy2.C6, R5.Pin_0
  N12: Teensy2.B6, R15.wiper
  N13: Teensy2.F7, R1.pin_0, R12.Pin_1
  N14: Teensy2.F6, R2.pin_0, R11.Pin_1
  N15: Teensy2.F5, R3.pin_0, R10.Pin_1
  N16: Teensy2.VCC, R1.pin_1, R2.pin_1, R3.pin_1, R13.Pin_0
  N17: LED5.anode, R9.Pin_1
  N18: R5.Pin_1, LED9.anode
  N19: R7.Pin_1, LED7.anode
  N20: R8.Pin_1, LED6.anode
  N21: R10.Pin_0, R11.Pin_0, R12.Pin_0, R15.leg2
  N22: R13.Pin_1, R15.leg1
  N23: R14.Pin_1, LED8.anode
